# Fritzing sketch 모터 (saved by Fritzing 0.9.3b)
breadboards: 1

parts:
  부품1 = Arduino Uno (Rev3)
  M1 = DC Motor  # not connected
  M2 = DC Motor  # not connected
  SmartDriveDuo10A1 = MDDS10
  VCC2 = 4 x AAA Battery Mount  # not connected
  VCC3 = 4 x AAA Battery Mount  # not connected
  BT1 = Bluetooth HC-06u [package=THT]
  부품2 = Bluetooth HM-10
  부품3 = Bluetooth HM-10
  부품4 = Bluetooth HM-10

nets:
  N1: 부품1.D8, 부품2.RXD
  N2: 부품1.D9_PWM, 부품2.TXD
  N3: 부품1.D10_PWM/SS, 부품3.RXD
  N4: 부품1.D11_PWM/MOSI, 부품3.TXD
  N5: 부품1.D12/MISO, 부품4.RXD
  N6: 부품1.D13/SCK, 부품4.TXD
  N7: 부품1.D2, SmartDriveDuo10A1.no_name_yet#connector_AN2
  N8: 부품1.D3_PWM, SmartDriveDuo10A1.no_name_yet#connector_AN1
  N9: 부품1.D4, SmartDriveDuo10A1.no_name_yet#connector_DIG2
  N10: 부품1.D5_PWM, SmartDriveDuo10A1.no_name_yet#connector_DIG1
  N11: 부품1.D6_PWM, BT1.RXD
  N12: 부품1.D7, BT1.TXD
  VCC: 부품1.5V, BT1.VCC, 부품2.VCC, 부품3.VCC, 부품4.VCC
  GND: 부품1.GND, SmartDriveDuo10A1.no_name_yet#connector_GND0, SmartDriveDuo10A1.no_name_yet#connector_V5, BT1.GND, 부품2.GND, 부품3.GND, 부품4.GND

custom parts:
  Bluetooth HC-06u: Bluetooth HC-06 - face up, pins down 16.5mm x 37.5mm PCB
