# Fritzing sketch 초음파 (saved by Fritzing 0.9.3b)
breadboards: 1

parts:
  hc-sr4 = hc-sr04
  hc-sr5 = hc-sr04
  hc-sr6 = hc-sr04
  부품1 = Arduino Uno (Rev3)
  hc-sr7 = hc-sr04
  hc-sr8 = hc-sr04
  hc-sr9 = hc-sr04

nets:
  VCC: hc-sr4.VCC, hc-sr5.VCC, hc-sr6.VCC, 부품1.5V, hc-sr7.VCC, hc-sr8.VCC, hc-sr9.VCC
  N1: hc-sr4.Trig, 부품1.D2
  N2: hc-sr4.Echo, 부품1.D3_PWM
  GND: hc-sr4.GND, hc-sr5.GND, hc-sr6.GND, 부품1.GND, hc-sr7.GND, hc-sr8.GND, hc-sr9.GND
  N3: hc-sr5.Trig, 부품1.D4
  N4: hc-sr5.Echo, 부품1.D5_PWM
  N5: hc-sr6.Trig, 부품1.D6_PWM
  N6: hc-sr6.Echo, 부품1.D7
  N7: 부품1.D8, hc-sr7.Echo
  N8: 부품1.D9_PWM, hc-sr7.Trig
  N9: 부품1.D10_PWM/SS, hc-sr8.Echo
  N10: 부품1.D11_PWM/MOSI, hc-sr8.Trig
  N11: 부품1.D12/MISO, hc-sr9.Echo
  N12: 부품1.D13/SCK, hc-sr9.Trig
