# Fritzing sketch 카메라 (saved by Fritzing 0.9.3b)
perfboards: 1
breadboards: 1

parts:
  부품1 = Arduino Uno (Rev3)
  R1 = Resistor [tolerance=±5% resistance=10 package=THT]  # not connected
  R2 = Resistor [tolerance=±5% resistance=4.7 package=THT]
  R3 = Resistor [tolerance=±5% resistance=4.7 package=THT]
  R4 = Resistor [tolerance=±5% resistance=10 package=THT]

nets:
  N1: 부품1.A5/SCL, R4.Pin_1
  N2: 부품1.D11_PWM/MOSI, R2.Pin_1, R3.Pin_1
  N3: 부품1.3V3, R4.Pin_0
  N4: 부품1.GND, R3.Pin_0

notes:
  GND
  HS
  SDA
  MCLK
  D6
  D4
  D2
  D0
  PWDN
  OV7670
  SCL
  D7
  D3
  PCLK
  3.3V
  RESET
  VS
  D5
  D1
